# Fritzing sketch test_circuit (saved by Fritzing 0.9.3b)
breadboards: 1

parts:
  M1 = STM32407VG Discovery
  YwRobot_Power_Supply1 = YwRobot Breadboard Power Supply [part_number=545043]
  C1 = Capacitor Polarized [package=cpol-radial-100uf-25v]
  C2 = Capacitor Polarized [package=cpol-radial-100uf-25v]
  LED1 = smd LED [color="Red (633nm)" package="1206 [SMD]"]
  R1 = Resistor [tolerance=±5% resistance=220 package=THT]
  LED2 = smd LED [color="Red (633nm)" package="1206 [SMD]"]
  R2 = Resistor [tolerance=±5% resistance=220 package=THT]
  LED3 = smd LED [color="Red (633nm)" package="1206 [SMD]"]
  R3 = Resistor [tolerance=±5% resistance=220 package=THT]
  U1 = POT [package=pot_mammoth]
  U2 = POT [package=pot_mammoth]
  U3 = POT [package=pot_mammoth]
  Part1 = USB converter CP2102
  U4 = ESP8266 WiFi Module [part_number=ESP8266]

nets:
  GND: M1.GND0, M1.GND-24, M1.GND-50, M1.GND-99, YwRobot_Power_Supply1.GND#13, YwRobot_Power_Supply1.GND#14, C1.-, U1.S, U2.S, U3.S, Part1.GND, U4.GND
  N1: M1.PE15, U4.TXD
  N2: M1.PA5, R2.Pin_0
  N3: M1.PA3, R1.Pin_0
  N4: M1.PA1, U2.A
  N5: M1.PB10, U4.RXD
  N6: M1.PA6, R3.Pin_0
  N7: M1.PA2, U3.A
  N8: M1.PA0, U1.A
  N9: M1.PD5, Part1.RXI
  N10: M1.PD6, Part1.TXO
  N11: YwRobot_Power_Supply1.VCC#5, YwRobot_Power_Supply1.VCC#6, C2.+
  N12: YwRobot_Power_Supply1.VCC#9, YwRobot_Power_Supply1.VCC#10, C1.+, U1.E, U2.E, U3.E, U4.CH_PD
  N13: YwRobot_Power_Supply1.GND#11, YwRobot_Power_Supply1.GND#12, C2.-, LED1.anode, LED2.anode, LED3.anode
  N14: LED1.cathode, R1.Pin_1
  N15: LED2.cathode, R2.Pin_1
  N16: LED3.cathode, R3.Pin_1

custom parts:
  STM32407VG Discovery: The STM32F4DISCOVERY Discovery kit allows users to easily develop applications with the STM32F407VG high performance microcontroller with the ARM® Cortex®-M4 32-bit core. It includes everything required either for beginners or for experienced users to get quickly started.Based on STM32F407VG, it includes an ST-LINK/V2 or ST-LINK/V2-A embedded debug tool, two ST-MEMS digital accelerometers, a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
  YwRobot Breadboard Power Supply: The YwRobot Breadboard Power Supply (MB-V2) has two power rails; they can be 5V or 3V3. Power to the module can be provided through the female USB socket or through the A10 (female) 2.1mm power jack.
  ESP8266 WiFi Module: Generic WiFi Module based on the ESP8266 with onboard PCB antenna and UART communications
